# Fritzing sketch schema (saved by Fritzing 0.9.3b)

parts:
  Componente1 = Arduino Nano (Rev3.0)
  Componente2 = NRF24L01+ Breakout Board
  KY-1 = Keyes Relay [package=THT]
  ZS-042_RTC1 = ZS-042 RTC Module
  U1 = LM2596 step down module
  KY-2 = Keyes Relay [package=THT]
  KY-3 = Keyes Relay [package=THT]
  KY-4 = Keyes Relay [package=THT]
  M1 = DC Motor
  M2 = DC Motor
  M3 = DC Motor
  M4 = DC Motor
  Componente3 = Arduino Nano (Rev3.0)
  Componente4 = NRF24L01+ Breakout Board
  KY-5 = Keyes Relay [package=THT]
  KY-6 = Keyes Relay [package=THT]
  ZS-042_RTC2 = ZS-042 RTC Module
  U2 = LM2596 step down module
  M8 = DC Motor
  KY-7 = Keyes Relay [package=THT]
  KY-8 = Keyes Relay [package=THT]
  M9 = DC Motor
  KY-9 = Keyes Relay [package=THT]
  KY-10 = Keyes Relay [package=THT]
  M10 = DC Motor
  KY-11 = Keyes Relay [package=THT]
  KY-12 = Keyes Relay [package=THT]
  M11 = DC Motor
  KY-13 = Keyes Relay [package=THT]
  Componente5 = Arduino Nano (Rev3.0)
  Componente6 = NRF24L01+ Breakout Board
  KY-14 = Keyes Relay [package=THT]
  KY-15 = Keyes Relay [package=THT]
  KY-16 = Keyes Relay [package=THT]
  KY-17 = Keyes Relay [package=THT]
  KY-18 = Keyes Relay [package=THT]
  KY-19 = Keyes Relay [package=THT]
  KY-20 = Keyes Relay [package=THT]
  KY-21 = Keyes Relay [package=THT]
  KY-22 = Keyes Relay [package=THT]
  ZS-042_RTC3 = ZS-042 RTC Module
  U3 = LM2596 step down module
  M12 = DC Motor
  M13 = DC Motor
  M14 = DC Motor
  M15 = DC Motor
  U4 = LM2596 step down module

nets:
  GND: Componente1.GND, Componente2.GND, KY-1.power, ZS-042_RTC1.GND, U1.OUT-, KY-2.power, KY-3.power, KY-4.power, M1.pin_1, M2.pin_1, M3.pin_1, M4.pin_1
  N1: Componente1.D2, KY-4.ground
  N2: Componente1.D3, KY-3.ground
  N3: Componente1.D4, KY-2.ground
  N4: Componente1.D5, KY-1.ground
  N5: Componente1.D7, Componente2.CE
  N6: Componente1.D8, Componente2.CS
  N7: Componente1.D10, Componente2.MISO
  N8: Componente1.D11/MOSI, Componente2.MOSI
  N9: Componente1.D12/MISO, Componente2.SCK
  N10: Componente1.VIN, KY-1.C, U1.OUT+, KY-2.C, KY-3.C, KY-4.C
  5V: Componente1.5V, KY-1.signal, ZS-042_RTC1.VCC, KY-2.signal, KY-3.signal, KY-4.signal
  N11: Componente1.A5, ZS-042_RTC1.SCL
  N12: Componente1.A4, ZS-042_RTC1.SDA
  3V3: Componente1.3V3, Componente2.VCC
  N13: KY-1.NC, M4.pin_2
  N14: KY-2.NC, M3.pin_2
  N15: KY-3.NC, M2.pin_2
  N16: KY-4.NC, M1.pin_2
  GND_2: Componente3.GND, Componente4.GND, KY-5.power, KY-5.NO, KY-6.power, KY-6.NC, ZS-042_RTC2.GND, U2.OUT-, KY-7.power, KY-7.NO, KY-8.power, KY-8.NC, KY-9.power, KY-9.NO, KY-10.power, KY-10.NC, KY-11.power, KY-11.NO, KY-12.power, KY-12.NC, KY-13.power
  N17: Componente3.D2, KY-5.ground, KY-6.ground
  N18: Componente3.D3, KY-7.ground, KY-8.ground
  N19: Componente3.D4, KY-9.ground, KY-10.ground
  N20: Componente3.D5, KY-11.ground, KY-12.ground
  N21: Componente3.D6, KY-13.ground
  N22: Componente3.D7, Componente4.CE
  N23: Componente3.D8, Componente4.CS
  N24: Componente3.D10, Componente4.MISO
  N25: Componente3.D11/MOSI, Componente4.MOSI
  N26: Componente3.D12/MISO, Componente4.SCK
  N27: Componente3.VIN, U2.OUT+, KY-13.NO
  5V_2: Componente3.5V, KY-5.signal, KY-6.signal, ZS-042_RTC2.VCC, KY-7.signal, KY-8.signal, KY-9.signal, KY-10.signal, KY-11.signal, KY-12.signal, KY-13.signal
  N28: Componente3.A5, ZS-042_RTC2.SCL
  N29: Componente3.A4, ZS-042_RTC2.SDA
  3V3_2: Componente3.3V3, Componente4.VCC
  N30: KY-5.NC, KY-6.NO, KY-7.NC, KY-8.NO, KY-9.NC, KY-10.NO, KY-11.NC, KY-12.NO, KY-13.C
  N31: KY-5.C, M8.pin_2
  N32: KY-6.C, M8.pin_1
  N33: KY-7.C, M9.pin_2
  N34: KY-8.C, M9.pin_1
  N35: KY-9.C, M10.pin_2
  N36: KY-10.C, M10.pin_1
  N37: KY-11.C, M11.pin_2
  N38: KY-12.C, M11.pin_1
  GND_3: Componente5.GND, Componente6.GND, KY-14.power, KY-15.power, KY-16.power, KY-17.power, KY-18.power, KY-19.power, KY-20.power, KY-21.power, KY-22.power, ZS-042_RTC3.GND, U4.OUT-
  N39: Componente5.D2, KY-21.ground, KY-22.ground
  N40: Componente5.D3, KY-19.ground, KY-20.ground
  N41: Componente5.D4, KY-17.ground, KY-18.ground
  N42: Componente5.D5, KY-15.ground, KY-16.ground
  N43: Componente5.D6, KY-14.ground
  N44: Componente5.D7, Componente6.CE
  N45: Componente5.D8, Componente6.CS
  N46: Componente5.D10, Componente6.MISO
  N47: Componente5.D11/MOSI, Componente6.MOSI
  N48: Componente5.D12/MISO, Componente6.SCK
  N49: Componente5.VIN, U4.OUT+
  5V_3: Componente5.5V, KY-14.signal, KY-15.signal, KY-16.signal, KY-17.signal, KY-18.signal, KY-19.signal, KY-20.signal, KY-21.signal, KY-22.signal, ZS-042_RTC3.VCC
  N50: Componente5.A5, ZS-042_RTC3.SCL
  N51: Componente5.A4, ZS-042_RTC3.SDA
  3V3_3: Componente5.3V3, Componente6.VCC
  N52: KY-14.C, KY-15.NO, KY-16.NC, KY-17.NO, KY-18.NC, KY-19.NO, KY-20.NC, KY-21.NO, KY-22.NC
  N53: KY-14.NO, U3.OUT+
  N54: KY-15.NC, KY-16.NO, KY-17.NC, KY-18.NO, KY-19.NC, KY-20.NO, KY-21.NC, KY-22.NO, U3.OUT-
  N55: KY-15.C, M12.pin_1
  N56: KY-16.C, M12.pin_2
  N57: KY-17.C, M13.pin_1
  N58: KY-18.C, M13.pin_2
  N59: KY-19.C, M14.pin_1
  N60: KY-20.C, M14.pin_2
  N61: KY-21.C, M15.pin_1
  N62: KY-22.C, M15.pin_2

notes:
  Relay con morsetti verso l'alto
  pin:
  VCC - GND - S
  In: 12V
  Out: 9V
  In: 12V
  Out: 5V

custom parts:
  Keyes Relay: The Keyes 5V relay module is suitable for SCM development, home appliance control. It uses a 5V~12V TIL control signal which can control DC / AC signal.
  LM2596 step down module: LM2596 DC-DC step down power supply module 3 A.
