# Fritzing sketch v1 (saved by Fritzing 0.9.3b)

parts:
  Componente3 = Arduino Nano (Rev3.0)
  Componente4 = NRF24L01+ Breakout Board
  KY-5 = Keyes Relay [package=THT]
  KY-6 = Keyes Relay [package=THT]
  KY-7 = Keyes Relay [package=THT]
  KY-8 = Keyes Relay [package=THT]
  ZS-042_RTC2 = ZS-042 RTC Module
  U2 = LM2596 step down module
  M5 = DC Motor
  M6 = DC Motor
  M7 = DC Motor
  M8 = DC Motor

nets:
  GND: Componente3.GND, Componente4.GND, KY-5.power, KY-6.power, KY-7.power, KY-8.power, ZS-042_RTC2.GND, U2.IN-, U2.OUT-, M5.pin_1, M6.pin_1, M7.pin_1, M8.pin_1
  N1: Componente3.D2, KY-5.ground
  N2: Componente3.D3, KY-6.ground
  N3: Componente3.D4, KY-7.ground
  N4: Componente3.D5, KY-8.ground
  N5: Componente3.D7, Componente4.CE
  N6: Componente3.D8, Componente4.CS
  N7: Componente3.D10, Componente4.MISO
  N8: Componente3.D11/MOSI, Componente4.MOSI
  N9: Componente3.D12/MISO, Componente4.SCK
  N10: Componente3.VIN, KY-5.C, KY-6.C, KY-7.C, KY-8.C, U2.OUT+
  5V: Componente3.5V, KY-5.signal, KY-6.signal, KY-7.signal, KY-8.signal, ZS-042_RTC2.VCC
  N11: Componente3.A5, ZS-042_RTC2.SCL
  N12: Componente3.A4, ZS-042_RTC2.SDA
  3V3: Componente3.3V3, Componente4.VCC
  N13: KY-5.NC, M8.pin_2
  N14: KY-6.NC, M7.pin_2
  N15: KY-7.NC, M6.pin_2
  N16: KY-8.NC, M5.pin_2

notes:
  In: 12V
  Out: 9V
  Relay con morsetti verso l'alto
  pin:
  VCC - GND - S

custom parts:
  Keyes Relay: The Keyes 5V relay module is suitable for SCM development, home appliance control. It uses a 5V~12V TIL control signal which can control DC / AC signal.
  LM2596 step down module: LM2596 DC-DC step down power supply module 3 A.
