# Fritzing sketch v2 (saved by Fritzing 0.9.3b)

parts:
  Componente4 = Arduino Nano (Rev3.0)
  KY-14 = Keyes Relay [package=THT]
  KY-15 = Keyes Relay [package=THT]
  KY-16 = Keyes Relay [package=THT]
  KY-17 = Keyes Relay [package=THT]
  KY-18 = Keyes Relay [package=THT]
  KY-19 = Keyes Relay [package=THT]
  KY-20 = Keyes Relay [package=THT]
  KY-21 = Keyes Relay [package=THT]
  KY-22 = Keyes Relay [package=THT]
  ZS-042_RTC3 = ZS-042 RTC Module
  U3 = LM2596 step down module
  M12 = DC Motor
  M13 = DC Motor
  M14 = DC Motor
  M15 = DC Motor

nets:
  GND: Componente4.GND, KY-14.power, KY-15.power, KY-15.NC, KY-16.power, KY-16.NO, KY-17.power, KY-17.NC, KY-18.power, KY-18.NO, KY-19.power, KY-19.NC, KY-20.power, KY-20.NO, KY-21.power, KY-21.NC, KY-22.power, KY-22.NO, ZS-042_RTC3.GND, U3.OUT-
  N1: Componente4.D2, KY-21.ground, KY-22.ground
  N2: Componente4.D3, KY-19.ground, KY-20.ground
  N3: Componente4.D4, KY-17.ground, KY-18.ground
  N4: Componente4.D5, KY-15.ground, KY-16.ground
  N5: Componente4.D6, KY-14.ground
  N6: Componente4.VIN, KY-14.NO, U3.OUT+
  5V: Componente4.5V, KY-14.signal, KY-15.signal, KY-16.signal, KY-17.signal, KY-18.signal, KY-19.signal, KY-20.signal, KY-21.signal, KY-22.signal, ZS-042_RTC3.VCC
  N7: Componente4.A5, ZS-042_RTC3.SCL
  N8: Componente4.A4, ZS-042_RTC3.SDA
  N9: KY-14.C, KY-15.NO, KY-16.NC, KY-17.NO, KY-18.NC, KY-19.NO, KY-20.NC, KY-21.NO, KY-22.NC
  N10: KY-15.C, M12.pin_1
  N11: KY-16.C, M12.pin_2
  N12: KY-17.C, M13.pin_1
  N13: KY-18.C, M13.pin_2
  N14: KY-19.C, M14.pin_1
  N15: KY-20.C, M14.pin_2
  N16: KY-21.C, M15.pin_1
  N17: KY-22.C, M15.pin_2

notes:
  In: 12V
  Out: 9V
  Relay con morsetti verso l'alto
  pin:
  VCC - GND - S

custom parts:
  Keyes Relay: The Keyes 5V relay module is suitable for SCM development, home appliance control. It uses a 5V~12V TIL control signal which can control DC / AC signal.
  LM2596 step down module: LM2596 DC-DC step down power supply module 3 A.
