# Fritzing sketch v3 (saved by Fritzing 0.9.3b)

parts:
  J2 = Power Jack [package=power_jack_pth_lock]
  Componente7 = Arduino Nano (Rev3.0)
  Componente8 = NRF24L01+ Breakout Board
  KY-25 = Keyes Relay [package=THT]  # not connected
  KY-26 = Keyes Relay [package=THT]
  KY-27 = Keyes Relay [package=THT]
  KY-28 = Keyes Relay [package=THT]
  KY-29 = Keyes Relay [package=THT]
  KY-30 = Keyes Relay [package=THT]
  KY-31 = Keyes Relay [package=THT]
  KY-32 = Keyes Relay [package=THT]
  KY-33 = Keyes Relay [package=THT]
  KY-34 = Keyes Relay [package=THT]
  KY-35 = Keyes Relay [package=THT]
  ZS-042_RTC4 = ZS-042 RTC Module
  U5 = LM2596 step down module
  U6 = LM2596 step down module
  M16 = DC Motor
  M17 = DC Motor
  M18 = DC Motor
  M19 = DC Motor

nets:
  GND: J2.GND, Componente7.GND, Componente8.GND, KY-26.power, KY-27.power, KY-28.power, KY-28.NC, KY-29.power, KY-29.NO, KY-30.power, KY-30.NC, KY-31.power, KY-31.NO, KY-32.power, KY-32.NC, KY-33.power, KY-33.NO, KY-34.power, KY-34.NC, KY-35.power, KY-35.NO, U5.IN-, U5.OUT-, U6.IN-, U6.OUT-
  N1: J2.PWR, U5.IN+, U6.IN+
  N2: Componente7.D2, KY-34.ground, KY-35.ground
  N3: Componente7.D3, KY-32.ground, KY-33.ground
  N4: Componente7.D4, KY-30.ground, KY-31.ground
  N5: Componente7.D5, KY-28.ground, KY-29.ground
  N6: Componente7.D7, Componente8.CE
  N7: Componente7.D8, Componente8.CS
  N8: Componente7.D9, KY-26.ground
  N9: Componente7.D10, KY-27.ground
  N10: Componente7.D11/MOSI, Componente8.MOSI
  N11: Componente7.D12/MISO, Componente8.MISO
  N12: Componente7.VIN, KY-26.signal, KY-27.signal, KY-28.signal, KY-29.signal, KY-30.signal, KY-31.signal, KY-32.signal, KY-33.signal, KY-34.signal, KY-35.signal, U5.OUT+
  5V: Componente7.5V, ZS-042_RTC4.VCC
  N13: Componente7.A5, ZS-042_RTC4.SCL
  N14: Componente7.A4, ZS-042_RTC4.SDA
  3V3: Componente7.3V3, Componente8.VCC
  N15: Componente7.D13/SCK, Componente8.SCK
  N16: KY-26.C, KY-30.NO, KY-31.NC, KY-34.NO, KY-35.NC
  N17: KY-26.NO, KY-27.NO, U6.OUT+
  N18: KY-27.C, KY-28.NO, KY-29.NC, KY-32.NO, KY-33.NC
  N19: KY-28.C, M16.pin_1
  N20: KY-29.C, M16.pin_2
  N21: KY-30.C, M17.pin_1
  N22: KY-31.C, M17.pin_2
  N23: KY-32.C, M18.pin_1
  N24: KY-33.C, M18.pin_2
  N25: KY-34.C, M19.pin_1
  N26: KY-35.C, M19.pin_2

notes:
  V4
  V3
  V2
  V1
  + - S
  In: 12V
  Out: 5V
  In: 12V
  Out: 9V

custom parts:
  Keyes Relay: The Keyes 5V relay module is suitable for SCM development, home appliance control. It uses a 5V~12V TIL control signal which can control DC / AC signal.
  LM2596 step down module: LM2596 DC-DC step down power supply module 3 A.
