# Fritzing sketch v4 (saved by Fritzing 0.9.3b)

parts:
  J2 = Power Jack [package=power_jack_pth_lock]
  Componente7 = Arduino Nano (Rev3.0)
  Componente8 = NRF24L01+ Breakout Board
  KY-25 = Keyes Relay [package=THT]  # not connected
  KY-26 = Keyes Relay [package=THT]
  KY-27 = Keyes Relay [package=THT]
  ZS-042_RTC4 = ZS-042 RTC Module
  U5 = LM2596 step down module
  U6 = LM2596 step down module
  M16 = DC Motor
  M17 = DC Motor
  M18 = DC Motor
  M19 = DC Motor
  8-Channel_Relay1 = 8-Channel 5v Relay Shield [package=relay-8ch5v10a]

nets:
  GND: J2.GND, Componente7.GND, Componente8.GND, KY-26.power, KY-27.power, ZS-042_RTC4.GND, U5.IN-, U5.OUT-, U6.IN-, U6.OUT-, 8-Channel_Relay1.GND, 8-Channel_Relay1.K1-On, 8-Channel_Relay1.K2-In, 8-Channel_Relay1.K3-On, 8-Channel_Relay1.K4-In, 8-Channel_Relay1.K5-On, 8-Channel_Relay1.K6-In, 8-Channel_Relay1.K7-On, 8-Channel_Relay1.K8-In
  N1: J2.PWR, U5.IN+, U6.IN+
  N2: Componente7.D2, 8-Channel_Relay1.IN7, 8-Channel_Relay1.IN8
  N3: Componente7.D3, 8-Channel_Relay1.IN5, 8-Channel_Relay1.IN6
  N4: Componente7.D4, 8-Channel_Relay1.IN3, 8-Channel_Relay1.IN4
  N5: Componente7.D5, 8-Channel_Relay1.IN1, 8-Channel_Relay1.IN2
  N6: Componente7.D7, Componente8.CE
  N7: Componente7.D8, Componente8.CS
  N8: Componente7.D9, KY-26.ground
  N9: Componente7.D10, KY-27.ground
  N10: Componente7.D11/MOSI, Componente8.MOSI
  N11: Componente7.D12/MISO, Componente8.MISO
  VIN: Componente7.VIN, KY-26.signal, KY-27.signal, U5.OUT+, 8-Channel_Relay1.VCC
  5V: Componente7.5V, ZS-042_RTC4.VCC
  N12: Componente7.A5, ZS-042_RTC4.SCL
  N13: Componente7.A4, ZS-042_RTC4.SDA
  3V3: Componente7.3V3, Componente8.VCC
  N14: Componente7.D13/SCK, Componente8.SCK
  N15: KY-26.C, 8-Channel_Relay1.K5-In, 8-Channel_Relay1.K6-On, 8-Channel_Relay1.K7-In, 8-Channel_Relay1.K8-On
  N16: KY-26.NO, KY-27.NO, U6.OUT+
  N17: KY-27.C, 8-Channel_Relay1.K1-In, 8-Channel_Relay1.K2-On, 8-Channel_Relay1.K3-In, 8-Channel_Relay1.K4-On
  N18: M16.pin_1, 8-Channel_Relay1.K1-Off
  N19: M16.pin_2, 8-Channel_Relay1.K2-Off
  N20: M17.pin_1, 8-Channel_Relay1.K3-Off
  N21: M17.pin_2, 8-Channel_Relay1.K4-Off
  N22: M18.pin_1, 8-Channel_Relay1.K5-Off
  N23: M18.pin_2, 8-Channel_Relay1.K6-Off
  N24: M19.pin_1, 8-Channel_Relay1.K7-Off
  N25: M19.pin_2, 8-Channel_Relay1.K8-Off

notes:
  V4
  V3
  V2
  V1
  + - S
  In: 12V
  Out: 5V
  In: 12V
  Out: 9V

custom parts:
  Keyes Relay: The Keyes 5V relay module is suitable for SCM development, home appliance control. It uses a 5V~12V TIL control signal which can control DC / AC signal.
  LM2596 step down module: LM2596 DC-DC step down power supply module 3 A.
  8-Channel 5v Relay Shield: 8 Channel 5v Relay Shield w. 2x SPD-06VDC-SD-C
